# Fritzing sketch experience 2 (saved by Fritzing 0.9.3b)
breadboards: 1

parts:
  Composant1 = Arduino Uno (Rev3)
  C1 = Ceramic Capacitor [capacitance=100nF package="100 mil [THT, multilayer]"]
  L1 = Inductor [package="400 mil [THT]"]
  R1 = Resistor [tolerance=±5% resistance=10k package=THT]
  R2 = Resistor [tolerance=±5% resistance=1M package=THT]
  C2 = Ceramic Capacitor [capacitance=0.1nF package="100 mil [THT, multilayer]"]
  R3 = Resistor [tolerance=±5% resistance=3.3k package=THT]
  D1 = Diode [package=sma-diode-kit]

nets:
  N1: Composant1.A0, C1.0, L1.pin_0, C2.1, D1.A, D1.C
  N2: Composant1.D9_PWM, R1.Pin_1
  N3: Composant1.GND, R2.Pin_0, C2.0
  electrode: C1.1
  N4: L1.pin_1, R1.Pin_0, R3.Pin_1
